// Logisim project Multiplexer.circ as structural Verilog: 1 circuit, main circuit main
module main (
  input  in_1,
  input  in_2,
  input  in_3,
  input  in_4,
  input  Enable,
  input  [1:0] Select_input,
  output out_7,
  output out_8,
  output out_9,
  output out_10
);

  wire multiplexer_1_out;

  Multiplexer #(.select(2)) multiplexer_1 (
    .in0(in_1), .in1(in_2), .in2(in_3), .in3(in_4), .out(multiplexer_1_out), .sel(Select_input), .en(Enable));
  LED led_1 (.in(multiplexer_1_out));
  Demultiplexer #(.select(2)) demultiplexer_1 (
    .out0(out_7), .out1(out_8), .out2(out_9), .out3(out_10), .in(multiplexer_1_out), .sel(Select_input),
    .en(Enable));
endmodule
